// Logisim project 8BitALU.circ as structural Verilog: 7 circuits, main circuit main
module main (
  input  Cin,
  input  [1:0] OP,
  input  Binv,
  input  Ainv,
  input  in_5,
  input  [7:0] A,
  input  [7:0] B,
  output [7:0] Output,
  output zero,
  output Over_Flow
);

  wire n1_bit_alu_1_overflow, n1_bit_alu_2_overflow, n1_bit_alu_3_overflow, n1_bit_alu_4_overflow,
       n1_bit_alu_5_overflow, n1_bit_alu_6_overflow, n1_bit_alu_7_overflow, or_1_out, xor_gate_1_xor;

  xor_gate xor_gate_1 (.A(Output[7]), .B(Over_Flow), .\xor (xor_gate_1_xor));
  _1_Bit_Alu u_1_bit_alu_1 (
    .Cin(Cin), .Op(OP), .Binv(Binv), .Ainv(Ainv), .A(A[0]), .B(B[0]), .SLT(xor_gate_1_xor), .Y(Output[0]),
    .OverFlow(n1_bit_alu_1_overflow));
  _1_Bit_Alu u_1_bit_alu_2 (
    .Cin(n1_bit_alu_1_overflow), .Op(OP), .Binv(Binv), .Ainv(Ainv), .A(A[1]), .B(B[1]), .SLT(in_5),
    .Y(Output[1]), .OverFlow(n1_bit_alu_2_overflow));
  _1_Bit_Alu u_1_bit_alu_3 (
    .Cin(n1_bit_alu_2_overflow), .Op(OP), .Binv(Binv), .Ainv(Ainv), .A(A[2]), .B(B[2]), .SLT(in_5),
    .Y(Output[2]), .OverFlow(n1_bit_alu_3_overflow));
  _1_Bit_Alu u_1_bit_alu_4 (
    .Cin(n1_bit_alu_3_overflow), .Op(OP), .Binv(Binv), .Ainv(Ainv), .A(A[3]), .B(B[3]), .SLT(in_5),
    .Y(Output[3]), .OverFlow(n1_bit_alu_4_overflow));
  _1_Bit_Alu u_1_bit_alu_5 (
    .Cin(n1_bit_alu_4_overflow), .Op(OP), .Binv(Binv), .Ainv(Ainv), .A(A[4]), .B(B[4]), .SLT(in_5),
    .Y(Output[4]), .OverFlow(n1_bit_alu_5_overflow));
  _1_Bit_Alu u_1_bit_alu_6 (
    .Cin(n1_bit_alu_5_overflow), .Op(OP), .Binv(Binv), .Ainv(Ainv), .A(A[5]), .B(B[5]), .SLT(in_5),
    .Y(Output[5]), .OverFlow(n1_bit_alu_6_overflow));
  _1_Bit_Alu u_1_bit_alu_7 (
    .Cin(n1_bit_alu_6_overflow), .Op(OP), .Binv(Binv), .Ainv(Ainv), .A(A[6]), .B(B[6]), .SLT(in_5),
    .Y(Output[6]), .OverFlow(n1_bit_alu_7_overflow));
  _1_Bit_Alu u_1_bit_alu_8 (
    .Cin(n1_bit_alu_7_overflow), .Op(OP), .Binv(Binv), .Ainv(Ainv), .A(A[7]), .B(B[7]), .SLT(in_5),
    .Y(Output[7]), .OverFlow(Over_Flow));
  or or_1 (or_1_out, Output[0], Output[1], Output[2], Output[3], Output[4], Output[5], Output[6], Output[7]);
  not not_1 (zero, or_1_out);

  // Notes on the sheet:
  //   8 Bit ALU
endmodule

// +
module _1_bit_adder (
  input  a,
  input  b,
  input  Cin,
  output Cout,
  output Sum
);

  wire and_1_out, and_2_out, and_3_out, and_4_out, and_5_out, and_6_out, and_7_out, not_1_out, not_2_out,
       not_3_out, not_4_out, not_5_out, not_6_out;

  and and_1 (and_1_out, b, Cin);
  and and_2 (and_2_out, a, Cin);
  and and_3 (and_3_out, a, b);
  not not_1 (not_1_out, a);
  and and_4 (and_4_out, not_1_out, not_2_out, Cin);
  not not_2 (not_2_out, b);
  not not_3 (not_3_out, a);
  and and_5 (and_5_out, not_3_out, b, not_4_out);
  not not_4 (not_4_out, Cin);
  and and_6 (and_6_out, a, not_5_out, not_6_out);
  not not_5 (not_5_out, b);
  not not_6 (not_6_out, Cin);
  and and_7 (and_7_out, a, b, Cin);
  or or_1 (Cout, and_1_out, and_2_out, and_3_out);
  or or_2 (Sum, and_4_out, and_5_out, and_6_out, and_7_out);

  // Notes on the sheet:
  //   1 Bit Adder
endmodule

// Mux
module _2_1_MUX (
  input  X,
  input  A,
  input  B,
  output Y
);

  wire and_1_out, and_2_out, not_1_out;

  not not_1 (not_1_out, X);
  and and_1 (and_1_out, not_1_out, A);
  and and_2 (and_2_out, X, B);
  or or_1 (Y, and_1_out, and_2_out);

  // Notes on the sheet:
  //   2 to 1 MUX
endmodule

module _2_4_decoder (
  input  s1,
  input  s0,
  output D3,
  output D2,
  output D1,
  output D0
);

  wire not_1_out, not_2_out, not_3_out, not_4_out;

  and and_1 (D3, s1, s0);
  not not_1 (not_1_out, s0);
  not not_2 (not_2_out, s1);
  not not_3 (not_3_out, s1);
  not not_4 (not_4_out, s0);
  and and_2 (D2, s1, not_1_out);
  and and_3 (D1, not_2_out, s0);
  and and_4 (D0, not_3_out, not_4_out);

  // Notes on the sheet:
  //   2 to 4 Decoder
endmodule

// Mux
module _4_1_mux (
  input  s1,
  input  s0,
  input  I3,
  input  I2,
  input  I1,
  input  I0,
  output y
);

  wire and_1_out, and_2_out, and_3_out, and_4_out, not_1_out, not_2_out, not_3_out, not_4_out;

  not not_1 (not_1_out, s0);
  not not_2 (not_2_out, s1);
  not not_3 (not_3_out, s0);
  not not_4 (not_4_out, s1);
  and and_1 (and_1_out, not_1_out, not_2_out, I3);
  and and_2 (and_2_out, not_3_out, s1, I2);
  and and_3 (and_3_out, s0, not_4_out, I1);
  and and_4 (and_4_out, s0, s1, I0);
  or or_1 (y, and_1_out, and_2_out, and_3_out, and_4_out);

  // Notes on the sheet:
  //   4 - 1 MUX
endmodule

module _1_Bit_Alu (
  input  Cin,
  input  [1:0] Op,
  input  Binv,
  input  Ainv,
  input  A,
  input  B,
  input  SLT,
  output Y,
  output OverFlow
);

  wire and_1_out, n1_bit_adder_1_sum, n2_1_mux_1_y, n2_1_mux_2_y, not_1_out, not_2_out, or_1_out;

  not not_1 (not_1_out, A);
  not not_2 (not_2_out, B);
  _2_1_MUX u_2_1_mux_1 (.X(Ainv), .A(A), .B(not_1_out), .Y(n2_1_mux_1_y));
  _2_1_MUX u_2_1_mux_2 (.X(Binv), .A(B), .B(not_2_out), .Y(n2_1_mux_2_y));
  and and_1 (and_1_out, n2_1_mux_1_y, n2_1_mux_2_y);
  or or_1 (or_1_out, n2_1_mux_1_y, n2_1_mux_2_y);
  _1_bit_adder u_1_bit_adder_1 (
    .a(n2_1_mux_1_y), .b(n2_1_mux_2_y), .Cin(Cin), .Cout(OverFlow), .Sum(n1_bit_adder_1_sum));
  _4_1_mux u_4_1_mux_1 (
    .s1(Op[0]), .s0(Op[1]), .I3(and_1_out), .I2(or_1_out), .I1(n1_bit_adder_1_sum), .I0(SLT), .y(Y));

  // Notes on the sheet:
  //   1 Bit ALU
endmodule

// Xor
module xor_gate (
  input  A,
  input  B,
  output \xor 
);

  wire and_1_out, and_2_out, not_1_out, not_2_out;

  not not_1 (not_1_out, A);
  not not_2 (not_2_out, B);
  and and_1 (and_1_out, not_1_out, B);
  and and_2 (and_2_out, A, not_2_out);
  or or_1 (\xor , and_1_out, and_2_out);

  // Notes on the sheet:
  //   XOR GATE
endmodule
